// Logisim project adding_pipeline_features.circ as structural Verilog: 6 circuits, main circuit 32-bit ALU
module main (
  input  in_1,
  input  in_2,
  output [31:0] IR,
  output [15:0] out_4
);

  wire and_1_out, and_2_out, clk, clr, flags_E, flags_GT, isAdd, isAnd, isAsr, isBeq, isBgt, isBranchTaken,
       isCall, isCmp, isDiv, isImmediate, isLd, isLsl, isLsr, isMod, isMov, isMul, isNot, isOr, isRet, isSt,
       isSub, isUBranch, isWb, Nop, not_1_out, not_2_out, Reset_out;
  wire [3:0] rd, rs1, rs2;
  wire [4:0] Opcode;
  wire [15:0] bit_extender_3_out, bit_extender_4_out, multiplexer_1_out, multiplexer_3_out, PC;
  wire [26:0] bitselector_1_out;
  wire [31:0] Alu_result, bit_extender_1_out, bit_extender_2_out, branchPC, branchTarget, CU_Out,
       demultiplexer_1_out1, immx, IRin, Ld_result, multiplexer_2_out, output1, output2, ram_1_data;

  Button Reset (.out(Reset_out));
  or or_1 (clr, in_1, Reset_out);
  OF of_1 (.in_1(IR), .out_2(rd), .out_5(rs1), .out_3(rs2), .out_4(Opcode), .out_7(immx), .out_6(isImmediate));
  BitSelector #(.width(32), .group(27)) bitselector_1 (.in(IR), .out(bitselector_1_out), .sel(in_2));
  // Probe on Alu_result
  Register #(.width(16)) register_1 (.D(multiplexer_1_out), .en(CU_Out[3]), .Q(PC), .clk(not_1_out), .clr(clr));
  not not_1 (not_1_out, clk);
  assign bit_extender_1_out = {{5{bitselector_1_out[26]}}, bitselector_1_out};  // Bit_Extender bit_extender_1
  assign bit_extender_2_out = {{16{1'b0}}, PC};  // Bit_Extender bit_extender_2
  _32_bit_ALU u_32_bit_alu_1 (
    .in_3(isAdd), .in_6(isSub), .in_9(isMul), .in_12(isDiv), .in_14(isMod), .in_4(isLsl), .in_7(isLsr),
    .in_10(isAsr), .in_13(isOr), .in_15(isAnd), .in_5(isNot), .in_8(isMov), .in_11(isCmp),
    .ALU_main_out(Alu_result), .in_1(output1), .in_2(multiplexer_2_out), .EnALU(CU_Out[5]), .in_16(clk));  // open: out_19
  Multiplexer #(.width(16), .enable("false")) multiplexer_1 (
    .in0(out_4), .in1(bit_extender_3_out), .out(multiplexer_1_out), .sel(isBranchTaken));
  Adder #(.width(32)) adder_1 (.a(bit_extender_1_out), .b(bit_extender_2_out), .out(branchTarget));  // open: cin, cout
  Adder #(.width(16)) adder_2 (.a(PC), .b(16'h1), .out(out_4));  // open: cin, cout
  Registers registers_1 (
    .Clock(clk), .op2(output2), .Clear(clr), .op1(output1), .in_2(rs2), .out_17({flags_GT, flags_E}),
    .in_3(Alu_result), .in_5(rs1), .in_6(rd), .in_15(isWb), .in_7(isSt), .in_8(isRet), .in_10(Ld_result),
    .in_11(isCall), .in_12(isLd), .in_13(PC), .in_14(isCmp), .Clear_2(CU_Out[6]));
  Multiplexer #(.width(32), .enable("false")) multiplexer_2 (
    .in0(output2), .in1(immx), .out(multiplexer_2_out), .sel(isImmediate));
  Bit_Extender #(.in_width(32)) bit_extender_3 (.in(branchPC), .out(bit_extender_3_out));
  CU cu_1 (
    .in_1(Opcode), .out_19(isMul), .out_12(isMod), .out_6(isAnd), .out_21(isNot), .out_7(isMov),
    .out_22(isLsr), .out_15(Nop), .out_9(isSt), .out_11(isSub), .out_5(isDiv), .out_20(isCmp), .out_13(isOr),
    .out_14(isLsl), .out_8(isAsr), .out_23(isLd), .out_16(isBeq), .out_24(isBgt), .out_17(isCall),
    .out_10(isUBranch), .out_25(isRet), .out_4(isAdd), .out_18(isWb), .in_3(clr), .out_27(CU_Out),
    .in_2({flags_GT, flags_E}), .out_26(clk));
  Bit_Extender #(.in_width(32)) bit_extender_4 (.in(Alu_result), .out(bit_extender_4_out));
  Multiplexer #(.width(16), .enable("false")) multiplexer_3 (
    .in0(bit_extender_4_out), .in1(PC), .out(multiplexer_3_out), .sel(CU_Out[0]));
  and and_1 (and_1_out, isBeq, flags_E);
  and and_2 (and_2_out, isBgt, flags_GT);
  not not_2 (not_2_out, CU_Out[2]);
  RAM #(.addrWidth(16), .dataWidth(32), .bus("separate")) ram_1 (
    .addr(multiplexer_3_out), .din(output2), .data(ram_1_data), .str(not_2_out), .sel(CU_Out[4]), .clk(clk),
    .ld(CU_Out[2]), .clr(clr));
  or or_2 (isBranchTaken, and_1_out, isUBranch, and_2_out);
  Register #(.width(32)) register_2 (.D(IRin), .en(CU_Out[1]), .Q(IR), .clk(clk), .clr(clr));
  Demultiplexer #(.width(32), .enable("false")) demultiplexer_1 (
    .out0(IRin), .out1(demultiplexer_1_out1), .in(ram_1_data), .sel(isLd));
  Register #(.width(32)) register_3 (.D(demultiplexer_1_out1), .en(isLd), .Q(Ld_result), .clk(clk), .clr(clr));
  Multiplexer #(.width(32), .enable("false")) multiplexer_4 (
    .in0(branchTarget), .in1(output1), .out(branchPC), .sel(isRet));

  // Other names for the same wires on the sheet: MUX_IF_Store = CU_Out[0]; enableIR = CU_Out[1]; MemLoad = CU_Out[2];
  //   enPC = CU_Out[3]; EnMemory = CU_Out[4]; EnAlu = CU_Out[5]; EnReg = CU_Out[6]

  // Notes on the sheet:
  //   PC Counter
endmodule

module _32_bit_ALU (
  input  [31:0] in_1,
  input  [31:0] in_2,
  input  in_3,
  input  in_4,
  input  in_5,
  input  in_6,
  input  in_7,
  input  in_8,
  input  in_9,
  input  in_10,
  input  in_11,
  input  in_12,
  input  in_13,
  input  in_14,
  input  in_15,
  input  in_16,
  input  EnALU,
  output [31:0] ALU_main_out,
  output out_19
);

  wire adder_subtractor_1_cout, and_2_out, comparator_2_gt, E, GT, undriven, undriven_2, undriven_3;
  wire [3:0] Opn;
  wire [4:0] B_27_31;
  wire [31:0] adder_subtractor_1_out_5, and_1_out, divider_1_out, divider_1_rem, multiplexer_1_out,
       multiplier_1_cout, multiplier_1_out, negator_1_out, or_1_out, shifter_1_out, shifter_2_out,
       shifter_3_out;

  Comparator #(.width(32), .mode("unsigned")) comparator_1 (.a(in_1), .b(in_2), .gt(GT), .eq(E));  // open: lt
  BitSelector #(.width(32), .group(5)) bitselector_1 (.in(in_2), .out(B_27_31), .sel(3'b000));
  Adder_Subtractor adder_subtractor_1 (
    .in_2(in_1), .in_1(in_2), .in_3(in_6), .out_5(adder_subtractor_1_out_5), .Cout(adder_subtractor_1_cout),
    .in_4(in_3));
  Multiplier #(.width(32)) multiplier_1 (
    .a(in_1), .b(in_2), .out(multiplier_1_out), .cout(multiplier_1_cout));  // open: cin
  Divider #(.width(32)) divider_1 (.a(in_1), .b(in_2), .out(divider_1_out), .rem(divider_1_rem));  // open: upper
  Shifter #(.width(32)) shifter_1 (.in(in_1), .\dist (B_27_31), .out(shifter_1_out));
  Shifter #(.width(32), .shift("lr")) shifter_2 (.in(in_1), .\dist (B_27_31), .out(shifter_2_out));
  Shifter #(.width(32), .shift("ar")) shifter_3 (.in(in_1), .\dist (B_27_31), .out(shifter_3_out));
  assign or_1_out = in_1 | in_2;  // OR_Gate or_1, 32 bits wide
  assign and_1_out = in_1 & in_2;  // AND_Gate and_1, 32 bits wide
  Negator #(.width(32)) negator_1 (.in(in_1), .out(negator_1_out));
  and and_2 (and_2_out, comparator_2_gt, in_9);
  Comparator #(.width(32), .mode("unsigned")) comparator_2 (
    .a(multiplier_1_cout), .b({32{1'b0}}), .gt(comparator_2_gt));  // open: eq, lt
  or or_2 (out_19, adder_subtractor_1_cout, and_2_out);
  Multiplexer #(.select(4), .width(32)) multiplexer_1 (
    .in0(adder_subtractor_1_out_5), .in1(adder_subtractor_1_out_5), .in2(multiplier_1_out),
    .in3(divider_1_out), .in4(divider_1_rem), .in5(shifter_1_out), .in6(shifter_2_out), .in7(shifter_3_out),
    .in8(or_1_out), .in9(and_1_out), .in10(negator_1_out), .in11(in_2), .in15({{30{1'b0}}, GT, E}),
    .out(multiplexer_1_out), .sel(Opn), .en(EnALU));  // open: in12, in13, in14
  Register #(.width(32), .trigger("falling")) register_1 (
    .D(multiplexer_1_out), .Q(ALU_main_out), .clk(in_16));  // open: en, clr
  Priority_Encoder #(.select(4)) priority_encoder_1 (
    .in0(in_3), .in1(in_6), .in2(in_9), .in3(in_12), .in4(in_14), .in5(in_4), .in6(in_7), .in7(in_10),
    .in8(in_13), .in9(in_15), .in10(in_5), .in11(in_8), .in12(undriven), .in13(undriven_2),
    .in14(undriven_3), .in15(in_11), .out(Opn), .en_in(1'b1));  // open: gs, en_out

  // Other names for the same wires on the sheet: A[31:0] = in_1; B[31:0] = in_2; clk = in_16; halt = out_19;
  //   isAdd = in_3; isAnd = in_15; isAsr = in_10; isCmp = in_11; isDiv = in_12; isLsl = in_4; isLsr = in_7;
  //   isMod = in_14; isMov = in_8; isMult = in_9; isNot = in_5; isOr = in_13; isSub = in_6

  // Notes on the sheet:
  //   Add/Sub
endmodule

module Adder_Subtractor (
  input  [31:0] in_1,
  input  [31:0] in_2,
  input  in_3,
  input  in_4,
  output [31:0] out_5,
  output Cout
);

  wire adder_1_cout;
  wire [31:0] multiplexer_1_out, not_1_out;

  assign not_1_out = ~in_2;  // NOT_Gate not_1, 32 bits wide
  Multiplexer #(.width(32), .enable("false")) multiplexer_1 (
    .in0(in_2), .in1(not_1_out), .out(multiplexer_1_out), .sel(in_3));
  Adder #(.width(32)) adder_1 (.a(in_1), .b(multiplexer_1_out), .out(out_5), .cin(in_3), .cout(adder_1_cout));
  and and_1 (Cout, adder_1_cout, in_4);

  // Other names for the same wires on the sheet: inA[31:0] = in_1; inB[31:0] = in_2; isAdd = in_4; isSub = in_3
endmodule

module Registers (
  input  Clock,
  input  [3:0] in_2,
  input  [31:0] in_3,
  input  Clear,
  input  [3:0] in_5,
  input  [3:0] in_6,
  input  in_7,
  input  in_8,
  input  Clear_2,
  input  [31:0] in_10,
  input  in_11,
  input  in_12,
  input  [15:0] in_13,
  input  in_14,
  input  in_15,
  output [31:0] op2,
  output [1:0] out_17,
  output [31:0] op1
);

  wire enR0, enR1, enR2, enR3, enR4, enR5, enR6, enR7, enR8, enR9, enR10, enR11, enR12, enR13, enR14, enR15;
  wire [1:0] bit_extender_2_out;
  wire [3:0] ReadPort_1, ReadPort_2, WritePort;
  wire [31:0] adder_1_out, bit_extender_1_out, R0out, R1out, R2out, R3out, R4out, R5out, R6out, R7out, R8out,
       R9out, R10out, R11out, R12out, R13out, R14out, R15out, result;

  Register #(.width(32), .trigger("falling")) register_1 (.D(result), .en(enR0), .Q(R0out), .clk(Clock), .clr(Clear));
  Register #(.width(32), .trigger("falling")) register_2 (.D(result), .en(enR4), .Q(R4out), .clk(Clock), .clr(Clear));
  Register #(.width(32), .trigger("falling")) register_3 (.D(result), .en(enR8), .Q(R8out), .clk(Clock), .clr(Clear));
  Register #(.width(32), .trigger("falling")) register_4 (.D(result), .en(enR12), .Q(R12out), .clk(Clock), .clr(Clear));
  Demultiplexer #(.select(4), .enable("false")) demultiplexer_1 (
    .out0(enR0), .out1(enR1), .out2(enR2), .out3(enR3), .out4(enR4), .out5(enR5), .out6(enR6), .out7(enR7),
    .out8(enR8), .out9(enR9), .out10(enR10), .out11(enR11), .out12(enR12), .out13(enR13), .out14(enR14),
    .out15(enR15), .in(in_15), .sel(WritePort));
  Multiplexer #(.width(4), .enable("false")) multiplexer_1 (.in0(in_5), .in1(4'b1111), .out(ReadPort_1), .sel(in_8));
  Multiplexer #(.width(4), .enable("false")) multiplexer_2 (.in0(in_2), .in1(in_6), .out(ReadPort_2), .sel(in_7));
  Register #(.width(32), .trigger("falling")) register_5 (.D(result), .en(enR1), .Q(R1out), .clk(Clock), .clr(Clear));
  Register #(.width(32), .trigger("falling")) register_6 (.D(result), .en(enR5), .Q(R5out), .clk(Clock), .clr(Clear));
  Register #(.width(32), .trigger("falling")) register_7 (.D(result), .en(enR9), .Q(R9out), .clk(Clock), .clr(Clear));
  Register #(.width(32), .trigger("falling")) register_8 (.D(result), .en(enR13), .Q(R13out), .clk(Clock), .clr(Clear));
  Multiplexer #(.select(4), .width(32)) multiplexer_3 (
    .in0(R0out), .in1(R1out), .in2(R2out), .in3(R3out), .in4(R4out), .in5(R5out), .in6(R6out), .in7(R7out),
    .in8(R8out), .in9(R9out), .in10(R10out), .in11(R11out), .in12(R12out), .in13(R13out), .in14(R14out),
    .in15(R15out), .out(op1), .sel(ReadPort_1), .en(Clear_2));
  Register #(.width(32), .trigger("falling")) register_9 (.D(result), .en(enR2), .Q(R2out), .clk(Clock), .clr(Clear));
  Register #(.width(32), .trigger("falling")) register_10 (.D(result), .en(enR6), .Q(R6out), .clk(Clock), .clr(Clear));
  Register #(.width(32), .trigger("falling")) register_11 (
    .D(result), .en(enR10), .Q(R10out), .clk(Clock), .clr(Clear));
  Register #(.width(32), .trigger("falling")) register_12 (
    .D(result), .en(enR14), .Q(R14out), .clk(Clock), .clr(Clear));
  Multiplexer #(.width(4), .enable("false")) multiplexer_4 (.in0(in_6), .in1(4'b1111), .out(WritePort), .sel(in_11));
  assign bit_extender_1_out = {{16{1'b0}}, in_13};  // Bit_Extender bit_extender_1
  Adder #(.width(32)) adder_1 (.a(bit_extender_1_out), .b(32'h1), .out(adder_1_out));  // open: cin, cout
  Register #(.width(32), .trigger("falling")) register_13 (.D(result), .en(enR3), .Q(R3out), .clk(Clock), .clr(Clear));
  Register #(.width(32), .trigger("falling")) register_14 (.D(result), .en(enR7), .Q(R7out), .clk(Clock), .clr(Clear));
  Register #(.width(32), .trigger("falling")) register_15 (
    .D(result), .en(enR11), .Q(R11out), .clk(Clock), .clr(Clear));
  Register #(.width(32), .trigger("falling")) register_16 (
    .D(result), .en(enR15), .Q(R15out), .clk(Clock), .clr(Clear));
  Multiplexer #(.select(4), .width(32)) multiplexer_5 (
    .in0(R0out), .in1(R1out), .in2(R2out), .in3(R3out), .in4(R4out), .in5(R5out), .in6(R6out), .in7(R7out),
    .in8(R8out), .in9(R9out), .in10(R10out), .in11(R11out), .in12(R12out), .in13(R13out), .in14(R14out),
    .in15(R15out), .out(op2), .sel(ReadPort_2), .en(Clear_2));
  // Probe on result
  Multiplexer #(.select(2), .width(32), .enable("false")) multiplexer_6 (
    .in0(in_3), .in1(in_10), .in2(adder_1_out), .out(result), .sel({in_11, in_12}));  // open: in3
  Bit_Extender #(.in_width(32), .out_width(2)) bit_extender_2 (.in(result), .out(bit_extender_2_out));
  Register #(.width(2), .trigger("high")) register_17 (
    .D(bit_extender_2_out), .en(in_14), .Q(out_17), .clk(Clock), .clr(Clear));

  // Other names for the same wires on the sheet: isLd = in_12; isCall = in_11; aluResult[31:0] = in_3; clk = Clock;
  //   clr = Clear; EnReg = Clear_2; flags_out[1:0] = out_17; isCmp = in_14; isRet = in_8; isSt = in_7; isWb = in_15;
  //   ldResult[31:0] = in_10; output1[31:0] = op1; output2[31:0] = op2; PC[15:0] = in_13; rd[3:0] = in_6;
  //   rs1_prime[3:0] = in_5; rs2[3:0] = in_2
endmodule

module CU (
  input  [4:0] in_1,
  input  [1:0] in_2,
  input  in_3,
  output out_4,
  output out_5,
  output out_6,
  output out_7,
  output out_8,
  output out_9,
  output out_10,
  output out_11,
  output out_12,
  output out_13,
  output out_14,
  output out_15,
  output out_16,
  output out_17,
  output out_18,
  output out_19,
  output out_20,
  output out_21,
  output out_22,
  output out_23,
  output out_24,
  output out_25,
  output out_26,
  output [31:0] out_27
);

  wire and_2_out, and_3_out, and_4_out, and_5_out, and_6_out, IsAddx, Isbranch, or_3_out, or_4_out, or_7_out,
       stage4, stage5;
  wire [2:0] Counter_q;

  Clock clock_1 (.out(out_26));
  Decoder #(.select(5), .enable("false")) decoder_1 (
    .out0(IsAddx), .out1(out_11), .out2(out_19), .out3(out_5), .out4(out_12), .out5(out_20), .out6(out_6),
    .out7(out_13), .out8(out_21), .out9(out_7), .out10(out_14), .out11(out_22), .out12(out_8),
    .out13(out_15), .out14(out_23), .out15(out_9), .out16(out_16), .out17(out_24), .out18(Isbranch),
    .out19(out_17), .out20(out_25), .sel(in_1));  // open: out21, out22, out23, out24, out25, out26, out27, out28, out29, out30, out31
  or or_1 (out_4, IsAddx, out_23, out_9);
  or or_2 (out_10, Isbranch, out_17, out_25);
  or or_3 (or_3_out, out_4, out_11, out_19, out_5, out_12, out_6, out_13, out_21, out_7, out_23, out_14, out_22, out_8, out_17);
  and and_1 (out_18, stage5, or_3_out);
  Decoder #(.select(3), .enable("false")) decoder_2 (
    .out0(out_27[1]), .out1(out_27[6]), .out2(out_27[5]), .out3(stage4), .out4(stage5), .sel(Counter_q));  // open: out5, out6, out7
  Counter #(.width(3), .max('h4)) Counter (.Q(Counter_q), .clk(out_26), .clr(in_3));  // open: load, D, count, carry
  or or_4 (or_4_out, out_23, out_9);
  and and_2 (and_2_out, stage4, or_4_out);
  and and_3 (and_3_out, stage4, out_23);
  or or_5 (out_27[4], out_27[1], and_2_out);
  or or_6 (out_27[2], out_27[1], and_3_out);
  and and_4 (and_4_out, out_16, in_2[0]);
  and and_5 (and_5_out, out_24, in_2[1]);
  or or_7 (or_7_out, and_4_out, and_5_out, out_10);
  and and_6 (and_6_out, or_7_out, stage4);
  or or_8 (out_27[3], and_6_out, out_27[6]);

  assign out_27[0] = out_27[1];

  // Other names for the same wires on the sheet: clk = out_26; clr = in_3; CU_Out[31:0] = {out_27[31:1], out_27[1]};
  //   EnIR = out_27[1]; IF_Store = out_27[1]; stage1 = out_27[1]; MemLoad = out_27[2]; enPC = out_27[3];
  //   EnMemory = out_27[4]; EnAlu = out_27[5]; stage3 = out_27[5]; EnReg = out_27[6]; stage2 = out_27[6];
  //   flags_E = in_2[0]; flags_GT = in_2[1]; IsAdd = out_4; IsAnd = out_6; IsAsr = out_8; IsBeq = out_16;
  //   IsBgt = out_24; IsCall = out_17; IsCmp = out_20; IsDiv = out_5; IsLd = out_23; isLsl = out_14; IsLsr = out_22;
  //   IsMod = out_12; IsMov = out_7; IsMul = out_19; IsNot = out_21; IsOr = out_13; IsRet = out_25; IsSt = out_9;
  //   IsSub = out_11; IsUBranch = out_10; IsWb = out_18; nop = out_15; opcode[4:0] = in_1
endmodule

module OF (
  input  [31:0] in_1,
  output [3:0] out_2,
  output [3:0] out_3,
  output [4:0] out_4,
  output [3:0] out_5,
  output out_6,
  output [31:0] out_7
);

  wire [31:0] bit_extender_1_out, bit_extender_2_out, shifter_1_out;

  assign bit_extender_1_out = {{16{1'b0}}, in_1[15:0]};  // Bit_Extender bit_extender_1
  assign bit_extender_2_out = {{16{in_1[15]}}, in_1[15:0]};  // Bit_Extender bit_extender_2
  // Probe on in_1[25:22]
  // Probe on in_1[17:14]
  Shifter #(.width(32)) shifter_1 (.in(bit_extender_1_out), .\dist (5'b10000), .out(shifter_1_out));
  // Probe on in_1[21:18]
  Multiplexer #(.select(2), .width(32), .enable("false")) multiplexer_1 (
    .in0(bit_extender_1_out), .in1(bit_extender_2_out), .in2(shifter_1_out), .out(out_7), .sel(in_1[17:16]));  // open: in3

  assign out_2 = in_1[25:22];
  assign out_3 = in_1[17:14];
  assign out_4 = in_1[31:27];
  assign out_5 = in_1[21:18];
  assign out_6 = in_1[26];

  // Other names for the same wires on the sheet: immediate[15:0] = in_1[15:0]; IR[31:0] = in_1;
  //   operand2_ad[3:0] = in_1[17:14]; rs2[3:0] = in_1[17:14]; immx[31:0] = out_7; IsImmediate = in_1[26];
  //   modifier[1:0] = in_1[17:16]; opcode[4:0] = in_1[31:27]; rd[3:0] = in_1[25:22]; rd_out[3:0] = in_1[25:22];
  //   operand1_ad[3:0] = in_1[21:18]; rs1[3:0] = in_1[21:18]
endmodule
