// Logisim project processor.circ as structural Verilog: 6 circuits, main circuit 32-bit ALU
module main (
  input  in_1,
  input  in_2,
  output [31:0] IR,
  output [15:0] out_4
);

  wire and_1_out, and_2_out, clk, clr, flags_E, flags_GT, isAdd, isAnd, isAsr, isBeq, isBgt, isBranchTaken,
       isCall, isCmp, isDiv, isImmediate, isLd, isLsl, isLsr, isMod, isMov, isMul, isNot, isOr, isRet, isSt,
       isSub, isUBranch, isWb, IsXnor, IsXor, Nop, not_1_out, not_2_out, not_3_out, not_4_out, or_2_out,
       register_2_q, Reset_out;
  wire [3:0] rd, rs1, rs2;
  wire [4:0] Opcode;
  wire [15:0] bit_extender_3_out, bit_extender_4_out, multiplexer_1_out, multiplexer_3_out, PC;
  wire [26:0] bitselector_1_out;
  wire [31:0] Alu_result, bit_extender_1_out, bit_extender_2_out, branchPC, branchTarget, immx, IRin,
       Ld_result, multiplexer_2_out, output1, output2, ram_1_data;

  Button Reset (.out(Reset_out));
  or or_1 (clr, in_1, Reset_out);
  OF of_1 (
    .in_2(IR), .out_3(rd), .out_6(rs1), .out_4(rs2), .out_5(Opcode), .out_8(immx), .out_7(isImmediate),
    .in_1(clk));
  BitSelector #(.width(32), .group(27)) bitselector_1 (.in(IR), .out(bitselector_1_out), .sel(in_2));
  Clock clock_1 (.out(clk));
  // Probe on output1
  Register #(.width(16)) register_1 (.D(multiplexer_1_out), .Q(PC), .clk(not_1_out), .clr(clr));  // open: en
  not not_1 (not_1_out, clk);
  assign bit_extender_1_out = {{5{bitselector_1_out[26]}}, bitselector_1_out};  // Bit_Extender bit_extender_1
  assign bit_extender_2_out = {{16{1'b0}}, PC};  // Bit_Extender bit_extender_2
  _32_bit_ALU u_32_bit_alu_1 (
    .in_3(isAdd), .in_6(isSub), .in_9(isMul), .in_12(isDiv), .in_15(isMod), .in_4(isLsl), .in_7(isLsr),
    .in_10(isAsr), .in_13(isOr), .in_16(isAnd), .in_5(isNot), .in_8(isMov), .in_11(isCmp),
    .ALU_main_out(Alu_result), .in_1(output1), .in_2(multiplexer_2_out), .in_14(IsXor), .in_17(IsXnor));
  Multiplexer #(.width(16), .enable("false")) multiplexer_1 (
    .in0(out_4), .in1(bit_extender_3_out), .out(multiplexer_1_out), .sel(isBranchTaken));
  Adder #(.width(32)) adder_1 (.a(bit_extender_1_out), .b(bit_extender_2_out), .out(branchTarget));  // open: cin, cout
  // Probe on output2
  Adder #(.width(16)) adder_2 (.a(PC), .b(16'h1), .out(out_4));  // open: cin, cout
  Registers registers_1 (
    .Clock(clk), .op2(output2), .Clear(clr), .op1(output1), .in_2(rs2), .out_16({flags_GT, flags_E}),
    .in_3(Alu_result), .in_5(rs1), .in_6(rd), .in_14(isWb), .in_7(isSt), .in_8(isRet), .in_9(Ld_result),
    .in_10(isCall), .in_11(isLd), .in_12(PC), .in_13(isCmp));
  Multiplexer #(.width(32), .enable("false")) multiplexer_2 (
    .in0(output2), .in1(immx), .out(multiplexer_2_out), .sel(isImmediate));
  Bit_Extender #(.in_width(32)) bit_extender_3 (.in(branchPC), .out(bit_extender_3_out));
  Bit_Extender #(.in_width(32)) bit_extender_4 (.in(Alu_result), .out(bit_extender_4_out));
  CU cu_1 (
    .in_1(Opcode), .out_20(isMul), .out_13(isMod), .out_7(isAnd), .out_22(isNot), .out_8(isMov),
    .out_23(isLsr), .out_16(Nop), .out_10(isSt), .out_12(isSub), .out_6(isDiv), .out_21(isCmp),
    .out_14(isOr), .out_15(isLsl), .out_9(isAsr), .out_24(isLd), .out_17(isBeq), .out_25(isBgt),
    .out_11(isCall), .out_3(isUBranch), .out_26(isRet), .out_5(isAdd), .out_19(isWb), .in_2(clk),
    .out_4(IsXor), .out_18(IsXnor));
  Multiplexer #(.width(16), .enable("false")) multiplexer_3 (
    .in0(PC), .in1(bit_extender_4_out), .out(multiplexer_3_out), .sel(or_2_out));
  or or_2 (or_2_out, isLd, isSt);
  and and_1 (and_1_out, isBeq, flags_E);
  and and_2 (and_2_out, isBgt, flags_GT);
  // Probe on bit_extender_4_out
  Register #(.width(1), .trigger("high")) register_2 (
    .D(isSt), .Q(register_2_q), .clk(clk), .clr(not_2_out));  // open: en
  not not_2 (not_2_out, clk);
  not not_3 (not_3_out, clk);
  RAM #(.addrWidth(16), .dataWidth(32), .bus("separate")) ram_1 (
    .addr(multiplexer_3_out), .din(output2), .data(ram_1_data), .str(register_2_q), .sel(1'b1),
    .clk(not_3_out), .ld(not_4_out), .clr(clr));
  not not_4 (not_4_out, register_2_q);
  or or_3 (isBranchTaken, and_1_out, isUBranch, and_2_out);
  Register #(.width(32)) register_3 (.D(IRin), .Q(IR), .clk(clk), .clr(clr));  // open: en
  Demultiplexer #(.width(32), .enable("false")) demultiplexer_1 (
    .out0(IRin), .out1(Ld_result), .in(ram_1_data), .sel(isLd));
  Multiplexer #(.width(32), .enable("false")) multiplexer_4 (
    .in0(branchTarget), .in1(output1), .out(branchPC), .sel(isRet));

  // Notes on the sheet:
  //   PC Counter
endmodule

module _32_bit_ALU (
  input  [31:0] in_1,
  input  [31:0] in_2,
  input  in_3,
  input  in_4,
  input  in_5,
  input  in_6,
  input  in_7,
  input  in_8,
  input  in_9,
  input  in_10,
  input  in_11,
  input  in_12,
  input  in_13,
  input  in_14,
  input  in_15,
  input  in_16,
  input  in_17,
  output [31:0] ALU_main_out
);

  wire E, GT, undriven;
  wire [3:0] Opn;
  wire [4:0] B_4_0;
  wire [31:0] adder_subtractor_1_out_5, and_1_out, divider_1_out, divider_1_rem, multiplier_1_out,
       negator_1_out, or_1_out, shifter_1_out, shifter_2_out, shifter_3_out, xnor_1_out, xor_1_out;

  Comparator #(.width(32), .mode("unsigned")) comparator_1 (.a(in_1), .b(in_2), .gt(GT), .eq(E));  // open: lt
  BitSelector #(.width(32), .group(5)) bitselector_1 (.in(in_2), .out(B_4_0), .sel(3'b000));
  Adder_Subtractor adder_subtractor_1 (
    .in_2(in_2), .in_1(in_1), .in_3(in_6), .out_5(adder_subtractor_1_out_5), .in_4(in_3));  // open: Cout
  Multiplier #(.width(32)) multiplier_1 (.a(in_1), .b(in_2), .out(multiplier_1_out));  // open: cin, cout
  Divider #(.width(32)) divider_1 (.a(in_1), .b(in_2), .out(divider_1_out), .rem(divider_1_rem));  // open: upper
  Shifter #(.width(32)) shifter_1 (.in(in_1), .\dist (B_4_0), .out(shifter_1_out));
  Shifter #(.width(32), .shift("lr")) shifter_2 (.in(in_1), .\dist (B_4_0), .out(shifter_2_out));
  Shifter #(.width(32), .shift("ar")) shifter_3 (.in(in_1), .\dist (B_4_0), .out(shifter_3_out));
  assign or_1_out = in_1 | in_2;  // OR_Gate or_1, 32 bits wide
  assign and_1_out = in_1 & in_2;  // AND_Gate and_1, 32 bits wide
  Negator #(.width(32)) negator_1 (.in(in_1), .out(negator_1_out));
  assign xor_1_out = in_1 ^ in_2;  // XOR_Gate xor_1, 32 bits wide
  assign xnor_1_out = ~(in_1 ^ in_2);  // XNOR_Gate xnor_1, 32 bits wide
  Multiplexer #(.select(4), .width(32), .enable("false")) multiplexer_1 (
    .in0(adder_subtractor_1_out_5), .in1(adder_subtractor_1_out_5), .in2(multiplier_1_out),
    .in3(divider_1_out), .in4(divider_1_rem), .in5(shifter_1_out), .in6(shifter_2_out), .in7(shifter_3_out),
    .in8(or_1_out), .in9(and_1_out), .in10(negator_1_out), .in11(in_2), .in12(xor_1_out), .in13(xnor_1_out),
    .in15({{30{1'b0}}, GT, E}), .out(ALU_main_out), .sel(Opn));  // open: in14
  Priority_Encoder #(.select(4)) priority_encoder_1 (
    .in0(in_3), .in1(in_6), .in2(in_9), .in3(in_12), .in4(in_15), .in5(in_4), .in6(in_7), .in7(in_10),
    .in8(in_13), .in9(in_16), .in10(in_5), .in11(in_8), .in12(in_14), .in13(in_17), .in14(undriven),
    .in15(in_11), .out(Opn), .en_in(1'b1));  // open: gs, en_out

  // Other names for the same wires on the sheet: A[31:0] = in_1; B[31:0] = in_2; isAdd = in_3; isAnd = in_16;
  //   isAsr = in_10; isCmp = in_11; isDiv = in_12; isLsl = in_4; isLsr = in_7; isMod = in_15; isMov = in_8;
  //   isMult = in_9; isNot = in_5; isOr = in_13; isSub = in_6; IsXnor = in_17; IsXor = in_14

  // Notes on the sheet:
  //   Add/Sub
endmodule

module Adder_Subtractor (
  input  [31:0] in_1,
  input  [31:0] in_2,
  input  in_3,
  input  in_4,
  output [31:0] out_5,
  output Cout
);

  wire adder_1_cout;
  wire [31:0] multiplexer_1_out, not_1_out;

  assign not_1_out = ~in_2;  // NOT_Gate not_1, 32 bits wide
  Multiplexer #(.width(32), .enable("false")) multiplexer_1 (
    .in0(in_2), .in1(not_1_out), .out(multiplexer_1_out), .sel(in_3));
  Adder #(.width(32)) adder_1 (.a(in_1), .b(multiplexer_1_out), .out(out_5), .cin(in_3), .cout(adder_1_cout));
  and and_1 (Cout, adder_1_cout, in_4);

  // Other names for the same wires on the sheet: inA[31:0] = in_1; inB[31:0] = in_2; isAdd = in_4; isSub = in_3
endmodule

module Registers (
  input  Clock,
  input  [3:0] in_2,
  input  [31:0] in_3,
  input  Clear,
  input  [3:0] in_5,
  input  [3:0] in_6,
  input  in_7,
  input  in_8,
  input  [31:0] in_9,
  input  in_10,
  input  in_11,
  input  [15:0] in_12,
  input  in_13,
  input  in_14,
  output [31:0] op2,
  output [1:0] out_16,
  output [31:0] op1
);

  wire enR0, enR1, enR2, enR3, enR4, enR5, enR6, enR7, enR8, enR9, enR10, enR11, enR12, enR13, enR14, enR15;
  wire [1:0] bit_extender_2_out;
  wire [3:0] ReadPort_1, ReadPort_2, WritePort;
  wire [31:0] adder_1_out, bit_extender_1_out, R0out, R1out, R2out, R3out, R4out, R5out, R6out, R7out, R8out,
       R9out, R10out, R11out, R12out, R13out, R14out, R15out, result;

  Register #(.width(32), .trigger("falling")) register_1 (.D(result), .en(enR0), .Q(R0out), .clk(Clock), .clr(Clear));
  Register #(.width(32), .trigger("falling")) register_2 (.D(result), .en(enR4), .Q(R4out), .clk(Clock), .clr(Clear));
  Register #(.width(32), .trigger("falling")) register_3 (.D(result), .en(enR8), .Q(R8out), .clk(Clock), .clr(Clear));
  Register #(.width(32), .trigger("falling")) register_4 (.D(result), .en(enR12), .Q(R12out), .clk(Clock), .clr(Clear));
  Demultiplexer #(.select(4), .enable("false")) demultiplexer_1 (
    .out0(enR0), .out1(enR1), .out2(enR2), .out3(enR3), .out4(enR4), .out5(enR5), .out6(enR6), .out7(enR7),
    .out8(enR8), .out9(enR9), .out10(enR10), .out11(enR11), .out12(enR12), .out13(enR13), .out14(enR14),
    .out15(enR15), .in(in_14), .sel(WritePort));
  Multiplexer #(.width(4), .enable("false")) multiplexer_1 (.in0(in_5), .in1(4'b1111), .out(ReadPort_1), .sel(in_8));
  Multiplexer #(.width(4), .enable("false")) multiplexer_2 (.in0(in_2), .in1(in_6), .out(ReadPort_2), .sel(in_7));
  Register #(.width(32), .trigger("falling")) register_5 (.D(result), .en(enR1), .Q(R1out), .clk(Clock), .clr(Clear));
  Register #(.width(32), .trigger("falling")) register_6 (.D(result), .en(enR5), .Q(R5out), .clk(Clock), .clr(Clear));
  Register #(.width(32), .trigger("falling")) register_7 (.D(result), .en(enR9), .Q(R9out), .clk(Clock), .clr(Clear));
  Register #(.width(32), .trigger("falling")) register_8 (.D(result), .en(enR13), .Q(R13out), .clk(Clock), .clr(Clear));
  Multiplexer #(.select(4), .width(32), .enable("false")) multiplexer_3 (
    .in0(R0out), .in1(R1out), .in2(R2out), .in3(R3out), .in4(R4out), .in5(R5out), .in6(R6out), .in7(R7out),
    .in8(R8out), .in9(R9out), .in10(R10out), .in11(R11out), .in12(R12out), .in13(R13out), .in14(R14out),
    .in15(R15out), .out(op1), .sel(ReadPort_1));
  Multiplexer #(.width(4), .enable("false")) multiplexer_4 (.in0(in_6), .in1(4'b1111), .out(WritePort), .sel(in_10));
  Register #(.width(32), .trigger("falling")) register_9 (.D(result), .en(enR2), .Q(R2out), .clk(Clock), .clr(Clear));
  Register #(.width(32), .trigger("falling")) register_10 (.D(result), .en(enR6), .Q(R6out), .clk(Clock), .clr(Clear));
  Register #(.width(32), .trigger("falling")) register_11 (
    .D(result), .en(enR10), .Q(R10out), .clk(Clock), .clr(Clear));
  Register #(.width(32), .trigger("falling")) register_12 (
    .D(result), .en(enR14), .Q(R14out), .clk(Clock), .clr(Clear));
  assign bit_extender_1_out = {{16{1'b0}}, in_12};  // Bit_Extender bit_extender_1
  Adder #(.width(32)) adder_1 (.a(bit_extender_1_out), .b(32'h1), .out(adder_1_out));  // open: cin, cout
  // Probe on in_3
  // Probe on in_9
  Register #(.width(32), .trigger("falling")) register_13 (.D(result), .en(enR3), .Q(R3out), .clk(Clock), .clr(Clear));
  Register #(.width(32), .trigger("falling")) register_14 (.D(result), .en(enR7), .Q(R7out), .clk(Clock), .clr(Clear));
  Register #(.width(32), .trigger("falling")) register_15 (
    .D(result), .en(enR11), .Q(R11out), .clk(Clock), .clr(Clear));
  Register #(.width(32), .trigger("falling")) register_16 (
    .D(result), .en(enR15), .Q(R15out), .clk(Clock), .clr(Clear));
  Multiplexer #(.select(4), .width(32), .enable("false")) multiplexer_5 (
    .in0(R0out), .in1(R1out), .in2(R2out), .in3(R3out), .in4(R4out), .in5(R5out), .in6(R6out), .in7(R7out),
    .in8(R8out), .in9(R9out), .in10(R10out), .in11(R11out), .in12(R12out), .in13(R13out), .in14(R14out),
    .in15(R15out), .out(op2), .sel(ReadPort_2));
  // Probe on result
  Multiplexer #(.select(2), .width(32), .enable("false")) multiplexer_6 (
    .in0(in_3), .in1(in_9), .in2(adder_1_out), .out(result), .sel({in_10, in_11}));  // open: in3
  Bit_Extender #(.in_width(32), .out_width(2)) bit_extender_2 (.in(result), .out(bit_extender_2_out));
  Register #(.width(2), .trigger("falling")) register_17 (
    .D(bit_extender_2_out), .en(in_13), .Q(out_16), .clk(Clock), .clr(Clear));

  // Other names for the same wires on the sheet: isLd = in_11; isCall = in_10; aluResult[31:0] = in_3; clk = Clock;
  //   clr = Clear; flags_out[1:0] = out_16; isCmp = in_13; isRet = in_8; isSt = in_7; isWb = in_14;
  //   ldResult[31:0] = in_9; output1[31:0] = op1; output2[31:0] = op2; PC[15:0] = in_12; rd[3:0] = in_6;
  //   rs1_prime[3:0] = in_5; rs2[3:0] = in_2
endmodule

module CU (
  input  [4:0] in_1,
  input  in_2,
  output out_3,
  output out_4,
  output out_5,
  output out_6,
  output out_7,
  output out_8,
  output out_9,
  output out_10,
  output out_11,
  output out_12,
  output out_13,
  output out_14,
  output out_15,
  output out_16,
  output out_17,
  output out_18,
  output out_19,
  output out_20,
  output out_21,
  output out_22,
  output out_23,
  output out_24,
  output out_25,
  output out_26
);

  wire decoder_1_out0, decoder_1_out1, decoder_1_out2, decoder_1_out3, decoder_1_out4, decoder_1_out5,
       decoder_1_out6, decoder_1_out7, decoder_1_out8, decoder_1_out9, decoder_1_out10, decoder_1_out11,
       decoder_1_out12, decoder_1_out13, decoder_1_out14, decoder_1_out15, decoder_1_out16, decoder_1_out17,
       decoder_1_out18, decoder_1_out19, decoder_1_out20, decoder_1_out21, decoder_1_out22, IsAddx, Isbranch;

  Decoder #(.select(5), .enable("false")) decoder_1 (
    .out0(decoder_1_out0), .out1(decoder_1_out1), .out2(decoder_1_out2), .out3(decoder_1_out3),
    .out4(decoder_1_out4), .out5(decoder_1_out5), .out6(decoder_1_out6), .out7(decoder_1_out7),
    .out8(decoder_1_out8), .out9(decoder_1_out9), .out10(decoder_1_out10), .out11(decoder_1_out11),
    .out12(decoder_1_out12), .out13(decoder_1_out13), .out14(decoder_1_out14), .out15(decoder_1_out15),
    .out16(decoder_1_out16), .out17(decoder_1_out17), .out18(decoder_1_out18), .out19(decoder_1_out19),
    .out20(decoder_1_out20), .out21(decoder_1_out21), .out22(decoder_1_out22), .sel(in_1));  // open: out23, out24, out25, out26, out27, out28, out29, out30, out31
  and and_1 (IsAddx, in_2, decoder_1_out0);
  and and_2 (out_12, in_2, decoder_1_out1);
  and and_3 (out_20, in_2, decoder_1_out2);
  and and_4 (out_6, in_2, decoder_1_out3);
  and and_5 (out_13, in_2, decoder_1_out4);
  and and_6 (out_21, in_2, decoder_1_out5);
  and and_7 (out_7, in_2, decoder_1_out6);
  and and_8 (out_14, in_2, decoder_1_out7);
  and and_9 (out_22, in_2, decoder_1_out8);
  and and_10 (out_8, in_2, decoder_1_out9);
  and and_11 (out_15, in_2, decoder_1_out10);
  and and_12 (out_23, in_2, decoder_1_out11);
  and and_13 (out_9, in_2, decoder_1_out12);
  and and_14 (out_16, in_2, decoder_1_out13);
  and and_15 (out_24, in_2, decoder_1_out14);
  and and_16 (out_10, in_2, decoder_1_out15);
  and and_17 (out_17, in_2, decoder_1_out16);
  and and_18 (out_25, in_2, decoder_1_out17);
  and and_19 (Isbranch, in_2, decoder_1_out18);
  and and_20 (out_11, in_2, decoder_1_out19);
  and and_21 (out_26, in_2, decoder_1_out20);
  and and_22 (out_4, in_2, decoder_1_out21);
  and and_23 (out_18, in_2, decoder_1_out22);
  or or_1 (out_5, IsAddx, out_24, out_10);
  or or_2 (out_3, Isbranch, out_11, out_26);
  or or_3 (out_19, out_4, out_5, out_12, out_20, out_6, out_13, out_7, out_14, out_22, out_8, out_24, out_15, out_23, out_9, out_11, out_18);

  // Other names for the same wires on the sheet: clk = in_2; IsAdd = out_5; IsAnd = out_7; IsAsr = out_9;
  //   IsBeq = out_17; IsBgt = out_25; IsCall = out_11; IsCmp = out_21; IsDiv = out_6; IsLd = out_24; isLsl = out_15;
  //   IsLsr = out_23; IsMod = out_13; IsMov = out_8; IsMul = out_20; IsNot = out_22; IsOr = out_14; IsRet = out_26;
  //   IsSt = out_10; IsSub = out_12; IsUBranch = out_3; IsWb = out_19; IsXnor = out_18; IsXor = out_4; nop = out_16;
  //   opcode[4:0] = in_1
endmodule

module OF (
  input  in_1,
  input  [31:0] in_2,
  output [3:0] out_3,
  output [3:0] out_4,
  output [4:0] out_5,
  output [3:0] out_6,
  output out_7,
  output [31:0] out_8
);

  wire [31:0] bit_extender_1_out, bit_extender_2_out, shifter_1_out;

  and and_1 (out_7, in_2[26], in_1);
  assign bit_extender_1_out = {{16{in_2[15]}}, in_2[15:0]};  // Bit_Extender bit_extender_1
  assign bit_extender_2_out = {{16{1'b0}}, in_2[15:0]};  // Bit_Extender bit_extender_2
  Shifter #(.width(32)) shifter_1 (.in(bit_extender_1_out), .\dist (5'b10000), .out(shifter_1_out));
  Multiplexer #(.select(2), .width(32), .enable("false")) multiplexer_1 (
    .in0(bit_extender_1_out), .in1(bit_extender_2_out), .in2(shifter_1_out), .out(out_8), .sel(in_2[17:16]));  // open: in3

  assign out_3 = in_2[25:22];
  assign out_4 = in_2[17:14];
  assign out_5 = in_2[31:27];
  assign out_6 = in_2[21:18];

  // Other names for the same wires on the sheet: clk = in_1; immediate[15:0] = in_2[15:0]; IR[31:0] = in_2;
  //   operand2_ad[3:0] = in_2[17:14]; rs2[3:0] = in_2[17:14]; immx[31:0] = out_8; IsImmediate = out_7;
  //   modifier[1:0] = in_2[17:16]; opcode[4:0] = in_2[31:27]; rd[3:0] = in_2[25:22]; rd_out[3:0] = in_2[25:22];
  //   operand1_ad[3:0] = in_2[21:18]; rs1[3:0] = in_2[21:18]
endmodule
